# Fritzing sketch Cardiac Memory [Sidney] (saved by Fritzing 0.9.3b)
breadboards: 1

parts:
  Arduino_Uno = Arduino Uno (Rev3) - ICSP
  LED_1 = smd LED [color="White (4500K)" package="1206 [SMD]"]
  LED_2 = smd LED [color="White (4500K)" package="1206 [SMD]"]
  LED_3 = smd LED [color="White (4500K)" package="1206 [SMD]"]
  LED_4 = smd LED [color="White (4500K)" package="1206 [SMD]"]
  R1 = Resistor [tolerance=±5% resistance=220 package="0402 [SMD]"]
  RL2 = Resistor [tolerance=±5% resistance=220 package="0402 [SMD]"]
  RL3 = Resistor [tolerance=±5% resistance=220 package="0402 [SMD]"]
  RL4 = Resistor [tolerance=±5% resistance=220 package="0402 [SMD]"]
  S1 = PHOTOCELL [package=photocell]
  S2 = PHOTOCELL [package=photocell]
  S3 = PHOTOCELL [package=photocell]
  S4 = PHOTOCELL [package=photocell]
  RS5 = Resistor [tolerance=±5% resistance=220 package="0402 [SMD]"]
  RS6 = Resistor [tolerance=±5% resistance=220 package="0402 [SMD]"]
  RS7 = Resistor [tolerance=±5% resistance=220 package="0402 [SMD]"]
  RS8 = Resistor [tolerance=±5% resistance=220 package="0402 [SMD]"]
  SP1 = SPEAKER [package=pcb_mount_speaker]
  LED_Green = smd LED [color="Green (555nm)" package="1206 [SMD]"]
  LED_Red = smd LED [color="Red (633nm)" package="1206 [SMD]"]
  R9 = Resistor [tolerance=±5% resistance=220 package="0402 [SMD]"]
  R10 = Resistor [tolerance=±5% resistance=220 package="0402 [SMD]"]

nets:
  N1: Arduino_Uno.A0, Arduino_Uno.A1, Arduino_Uno.A2, Arduino_Uno.A3, Arduino_Uno.5V, RS5.Pin_0, RS6.Pin_0, RS7.Pin_0, RS8.Pin_0
  N2: Arduino_Uno.D13/SCK, SP1.-
  N3: Arduino_Uno.GND, LED_1.cathode, LED_2.cathode, LED_3.cathode, LED_4.cathode, S1.P$1, S2.P$1, S3.P$1, S4.P$1, SP1.+, LED_Green.cathode, LED_Red.cathode
  N4: Arduino_Uno.D2, R10.Pin_0
  N5: Arduino_Uno.D3_PWM, R9.Pin_0
  N6: Arduino_Uno.D4, RL4.Pin_1
  N7: Arduino_Uno.D5_PWM, RL3.Pin_1
  N8: Arduino_Uno.D6_PWM, RL2.Pin_1
  N9: Arduino_Uno.D7, R1.Pin_1
  N10: LED_1.anode, R1.Pin_0
  N11: LED_2.anode, RL2.Pin_0
  N12: LED_3.anode, RL3.Pin_0
  N13: LED_4.anode, RL4.Pin_0
  N14: S1.P$2, RS5.Pin_1
  N15: S2.P$2, RS6.Pin_1
  N16: S3.P$2, RS7.Pin_1
  N17: S4.P$2, RS8.Pin_1
  N18: LED_Green.anode, R9.Pin_1
  N19: LED_Red.anode, R10.Pin_1
